// Logisim project Exercicio1.circ as structural Verilog: 1 circuit, main circuit main
module main (
  input  in_1,
  input  in_2
);

  wire clock_1_out, j_k_ff_1_q, j_k_ff_2_q, j_k_ff_3_q, j_k_ff_4_q, j_k_ff_5_q;

  Clock clock_1 (.out(clock_1_out));
  // Probe on j_k_ff_1_q
  J_K_Flip_Flop j_k_ff_1 (.J(in_1), .clk(j_k_ff_2_q), .K(in_1), .Q(j_k_ff_1_q), .reset(in_2));  // open: Qn, preset
  // Probe on j_k_ff_2_q
  J_K_Flip_Flop j_k_ff_2 (.J(in_1), .clk(j_k_ff_3_q), .K(in_1), .Q(j_k_ff_2_q), .reset(in_2));  // open: Qn, preset
  // Probe on j_k_ff_3_q
  J_K_Flip_Flop j_k_ff_3 (.J(in_1), .clk(j_k_ff_4_q), .K(in_1), .Q(j_k_ff_3_q), .reset(in_2));  // open: Qn, preset
  // Probe on j_k_ff_4_q
  J_K_Flip_Flop j_k_ff_4 (.J(in_1), .clk(j_k_ff_5_q), .K(in_1), .Q(j_k_ff_4_q), .reset(in_2));  // open: Qn, preset
  // Probe on j_k_ff_5_q
  J_K_Flip_Flop j_k_ff_5 (.J(in_1), .clk(clock_1_out), .K(in_1), .Q(j_k_ff_5_q), .reset(in_2));  // open: Qn, preset
endmodule
