// Logisim project Exercicio2.circ as structural Verilog: 1 circuit, main circuit main
module main (
  input  in_1,
  input  in_2
);

  wire clock_1_out, j_k_ff_1_qn, j_k_ff_2_qn, j_k_ff_3_qn, j_k_ff_4_qn, j_k_ff_5_qn;

  Clock clock_1 (.out(clock_1_out));
  // Probe on j_k_ff_1_qn
  J_K_Flip_Flop j_k_ff_1 (.J(in_1), .clk(j_k_ff_2_qn), .K(in_1), .Qn(j_k_ff_1_qn), .reset(in_2));  // open: Q, preset
  // Probe on j_k_ff_2_qn
  J_K_Flip_Flop j_k_ff_2 (.J(in_1), .clk(j_k_ff_3_qn), .K(in_1), .Qn(j_k_ff_2_qn), .reset(in_2));  // open: Q, preset
  // Probe on j_k_ff_3_qn
  J_K_Flip_Flop j_k_ff_3 (.J(in_1), .clk(j_k_ff_4_qn), .K(in_1), .Qn(j_k_ff_3_qn), .reset(in_2));  // open: Q, preset
  // Probe on j_k_ff_4_qn
  J_K_Flip_Flop j_k_ff_4 (.J(in_1), .clk(j_k_ff_5_qn), .K(in_1), .Qn(j_k_ff_4_qn), .reset(in_2));  // open: Q, preset
  // Probe on j_k_ff_5_qn
  J_K_Flip_Flop j_k_ff_5 (.J(in_1), .clk(clock_1_out), .K(in_1), .Qn(j_k_ff_5_qn), .reset(in_2));  // open: Q, preset
endmodule
