// Logisim project Exercicio3.circ as structural Verilog: 1 circuit, main circuit main
module main (
  input  in_1,
  input  in_2
);

  wire clock_1_out, j_k_ff_1_q, j_k_ff_1_qn, j_k_ff_2_q, j_k_ff_2_qn, j_k_ff_3_q, j_k_ff_3_qn, j_k_ff_4_q,
       j_k_ff_4_qn, j_k_ff_5_q, nand_1_out, nand_2_out, not_1_out, not_3_out;

  Clock clock_1 (.out(clock_1_out));
  nand nand_1 (nand_1_out, in_2, nand_2_out);
  not not_1 (not_1_out, j_k_ff_1_q);
  nand nand_2 (nand_2_out, not_1_out, j_k_ff_2_q, j_k_ff_4_q, not_3_out);
  // NOT_Gate not_2 has open pins: in=j_k_ff_3_q, out=open
  not not_3 (not_3_out, j_k_ff_5_q);
  // Probe on j_k_ff_5_q
  J_K_Flip_Flop #(.Pre_Clr_Positions("LEGACY"), .enable("true")) j_k_ff_1 (
    .J(in_1), .clk(clock_1_out), .K(in_1), .Q(j_k_ff_1_q), .Qn(j_k_ff_1_qn), .reset(nand_1_out));  // open: preset, en
  // Probe on j_k_ff_4_q
  J_K_Flip_Flop #(.Pre_Clr_Positions("LEGACY"), .enable("true")) j_k_ff_2 (
    .J(in_1), .clk(j_k_ff_1_qn), .K(in_1), .Q(j_k_ff_2_q), .Qn(j_k_ff_2_qn), .reset(nand_1_out));  // open: preset, en
  // Probe on j_k_ff_3_q
  J_K_Flip_Flop #(.Pre_Clr_Positions("LEGACY"), .enable("true")) j_k_ff_3 (
    .J(in_1), .clk(j_k_ff_2_qn), .K(in_1), .Q(j_k_ff_3_q), .Qn(j_k_ff_3_qn), .reset(nand_1_out));  // open: preset, en
  // Probe on j_k_ff_2_q
  J_K_Flip_Flop #(.Pre_Clr_Positions("LEGACY"), .enable("true")) j_k_ff_4 (
    .J(in_1), .clk(j_k_ff_3_qn), .K(in_1), .Q(j_k_ff_4_q), .Qn(j_k_ff_4_qn), .reset(nand_1_out));  // open: preset, en
  // Probe on j_k_ff_1_q
  J_K_Flip_Flop #(.Pre_Clr_Positions("LEGACY"), .enable("true")) j_k_ff_5 (
    .J(in_1), .clk(j_k_ff_4_qn), .K(in_1), .Q(j_k_ff_5_q), .reset(nand_1_out));  // open: Qn, preset, en
endmodule
