// Logisim project Exercicio4.circ as structural Verilog: 1 circuit, main circuit main
module main (
  input  in_1,
  input  in_2
);

  wire and_1_out, clock_1_out, j_k_ff_1_q, j_k_ff_1_qn, j_k_ff_2_q, j_k_ff_2_qn, j_k_ff_3_q, j_k_ff_3_qn,
       j_k_ff_4_q, j_k_ff_4_qn, j_k_ff_5_q, j_k_ff_5_qn, not_1_out, not_2_out, not_3_out, not_4_out, or_1_out;

  Clock clock_1 (.out(clock_1_out));
  not not_1 (not_1_out, in_1);
  or or_1 (or_1_out, not_1_out, and_1_out);
  not not_2 (not_2_out, j_k_ff_1_qn);
  and and_1 (and_1_out, not_2_out, j_k_ff_2_qn, not_3_out, j_k_ff_4_qn, not_4_out);
  not not_3 (not_3_out, j_k_ff_3_qn);
  not not_4 (not_4_out, j_k_ff_5_qn);
  // Probe on j_k_ff_5_q
  J_K_Flip_Flop #(.Pre_Clr_Positions("LEGACY"), .enable("true")) j_k_ff_1 (
    .J(in_1), .clk(clock_1_out), .K(in_1), .Q(j_k_ff_1_q), .Qn(j_k_ff_1_qn), .preset(or_1_out), .reset(in_2));  // open: en
  // Probe on j_k_ff_4_q
  J_K_Flip_Flop #(.Pre_Clr_Positions("LEGACY"), .enable("true")) j_k_ff_2 (
    .J(in_1), .clk(j_k_ff_1_q), .K(in_1), .Q(j_k_ff_2_q), .Qn(j_k_ff_2_qn), .preset(or_1_out), .reset(in_2));  // open: en
  // Probe on j_k_ff_3_q
  J_K_Flip_Flop #(.Pre_Clr_Positions("LEGACY"), .enable("true")) j_k_ff_3 (
    .J(in_1), .clk(j_k_ff_2_q), .K(in_1), .Q(j_k_ff_3_q), .Qn(j_k_ff_3_qn), .preset(or_1_out), .reset(in_2));  // open: en
  // Probe on j_k_ff_2_q
  J_K_Flip_Flop #(.Pre_Clr_Positions("LEGACY"), .enable("true")) j_k_ff_4 (
    .J(in_1), .clk(j_k_ff_3_q), .K(in_1), .Q(j_k_ff_4_q), .Qn(j_k_ff_4_qn), .preset(or_1_out), .reset(in_2));  // open: en
  // Probe on j_k_ff_1_q
  J_K_Flip_Flop #(.Pre_Clr_Positions("LEGACY"), .enable("true")) j_k_ff_5 (
    .J(in_1), .clk(j_k_ff_4_q), .K(in_1), .Q(j_k_ff_5_q), .Qn(j_k_ff_5_qn), .preset(or_1_out), .reset(in_2));  // open: en
endmodule
