// Logisim project Exercicio5.circ as structural Verilog: 1 circuit, main circuit main
module main (
  input  in_1
);

  wire and_1_out, clock_1_out, not_1_out, not_2_out, or_1_out, t_ff_1_q, t_ff_2_q, t_ff_2_qn, t_ff_3_q,
       t_ff_3_qn, t_ff_4_q, t_ff_4_qn;

  Clock clock_1 (.out(clock_1_out));
  or or_1 (or_1_out, in_1, and_1_out);
  // Probe on t_ff_1_q
  T_Flip_Flop t_ff_1 (.clk(t_ff_2_qn), .T(t_ff_2_qn), .Q(t_ff_1_q), .reset(or_1_out));  // open: Qn, preset
  not not_1 (not_1_out, t_ff_2_q);
  and and_1 (and_1_out, t_ff_1_q, not_1_out, t_ff_3_q, not_2_out);
  not not_2 (not_2_out, t_ff_4_q);
  // Probe on t_ff_2_q
  T_Flip_Flop t_ff_2 (.clk(t_ff_3_qn), .T(t_ff_3_qn), .Q(t_ff_2_q), .Qn(t_ff_2_qn), .reset(or_1_out));  // open: preset
  // Probe on t_ff_3_q
  T_Flip_Flop t_ff_3 (.clk(t_ff_4_qn), .T(t_ff_4_qn), .Q(t_ff_3_q), .Qn(t_ff_3_qn), .reset(or_1_out));  // open: preset
  // Probe on t_ff_4_q
  T_Flip_Flop t_ff_4 (
    .clk(clock_1_out), .T(clock_1_out), .Q(t_ff_4_q), .Qn(t_ff_4_qn), .reset(or_1_out));  // open: preset
endmodule
