// Logisim project Exercicio7.circ as structural Verilog: 1 circuit, main circuit main
module main (
  input  in_1,
  input  in_2
);

  wire clock_1_out, j_k_ff_1_q, j_k_ff_2_q, j_k_ff_3_q, j_k_ff_4_q, j_k_ff_5_q, j_k_ff_5_qn, not_1_out,
       not_2_out, not_3_out, not_4_out, not_5_out, or_1_out;

  Clock clock_1 (.out(clock_1_out));
  or or_1 (or_1_out, j_k_ff_5_qn, in_1);
  not not_1 (not_1_out, or_1_out);
  // Probe on j_k_ff_1_q
  J_K_Flip_Flop j_k_ff_1 (
    .J(or_1_out), .clk(clock_1_out), .K(not_1_out), .Q(j_k_ff_1_q), .reset(in_2));  // open: Qn, preset
  not not_2 (not_2_out, j_k_ff_1_q);
  // Probe on j_k_ff_2_q
  J_K_Flip_Flop j_k_ff_2 (
    .J(j_k_ff_1_q), .clk(clock_1_out), .K(not_2_out), .Q(j_k_ff_2_q), .reset(in_2));  // open: Qn, preset
  // Probe on j_k_ff_3_q
  J_K_Flip_Flop j_k_ff_3 (
    .J(j_k_ff_2_q), .clk(clock_1_out), .K(not_3_out), .Q(j_k_ff_3_q), .reset(in_2));  // open: Qn, preset
  not not_3 (not_3_out, j_k_ff_2_q);
  not not_4 (not_4_out, j_k_ff_3_q);
  // Probe on j_k_ff_4_q
  J_K_Flip_Flop j_k_ff_4 (
    .J(j_k_ff_3_q), .clk(clock_1_out), .K(not_4_out), .Q(j_k_ff_4_q), .reset(in_2));  // open: Qn, preset
  not not_5 (not_5_out, j_k_ff_4_q);
  // Probe on j_k_ff_5_q
  J_K_Flip_Flop j_k_ff_5 (
    .J(j_k_ff_4_q), .clk(clock_1_out), .K(not_5_out), .Q(j_k_ff_5_q), .Qn(j_k_ff_5_qn), .reset(in_2));  // open: preset
endmodule
