// Logisim project Complemento 1.circ as structural Verilog: 2 circuits, main circuit main
module main (
  input  [7:0] in_1,
  output [7:0] out_2
);

  not not_1 (out_2[7], in_1[7]);
  not not_2 (out_2[4], in_1[4]);
  not not_3 (out_2[6], in_1[6]);
  not not_4 (out_2[5], in_1[5]);
  not not_5 (out_2[2], in_1[2]);
  not not_6 (out_2[1], in_1[1]);
  not not_7 (out_2[3], in_1[3]);
  not not_8 (out_2[0], in_1[0]);
endmodule

module Complemento (
  input  in_1,
  input  in_2,
  input  in_3,
  input  in_4,
  input  in_5,
  input  in_6,
  input  in_7,
  output out_8,
  output out_9,
  output out_10,
  output out_11,
  output out_12,
  output out_13,
  output out_14
);

  // main main_1: pin names not known; wires that end beside it: in_1, out_8, in_2, out_9, in_3, out_10
endmodule
