// Logisim project Complemento de 2.circ as structural Verilog: 2 circuits, main circuit main
module main (
  input  in_1,
  input  in_2,
  input  in_3,
  output out_4,
  output out_5
);

  wire and_1_out, and_2_out, and_3_out, xor_1_out;

  xor xor_1 (xor_1_out, in_1, in_2);
  and and_1 (and_1_out, in_2, in_3);
  and and_2 (and_2_out, in_3, in_1);
  and and_3 (and_3_out, in_2, in_1);
  xor xor_2 (out_4, xor_1_out, in_3);
  or or_1 (out_5, and_1_out, and_2_out, and_3_out);
endmodule

module Somador (
  input  in_1,
  input  in_2,
  input  in_3,
  input  in_4,
  input  in_5,
  input  in_6,
  input  in_7,
  input  in_8,
  input  in_9,
  input  in_10,
  input  in_11,
  input  in_12,
  input  in_13,
  input  in_14,
  input  in_15,
  input  in_16,
  input  in_17,
  output out_18,
  output out_19,
  output out_20,
  output out_21,
  output out_22,
  output out_23,
  output out_24,
  output out_25,
  output out_26
);

  wire main_2_out_5, main_3_out_5, main_4_out_5, main_5_out_5, main_6_out_5, main_7_out_5, main_8_out_5;

  main main_1 (.in_1(in_9), .in_2(in_1), .in_3(main_2_out_5), .out_4(out_19), .out_5(out_18));
  main main_2 (.in_1(in_10), .in_2(in_2), .in_3(main_3_out_5), .out_4(out_20), .out_5(main_2_out_5));
  main main_3 (.in_1(in_11), .in_2(in_3), .in_3(main_4_out_5), .out_4(out_21), .out_5(main_3_out_5));
  main main_4 (.in_1(in_12), .in_2(in_4), .in_3(main_6_out_5), .out_4(out_22), .out_5(main_4_out_5));
  main main_5 (.in_1(in_14), .in_2(in_6), .in_3(main_7_out_5), .out_4(out_24), .out_5(main_5_out_5));
  main main_6 (.in_1(in_13), .in_2(in_5), .in_3(main_5_out_5), .out_4(out_23), .out_5(main_6_out_5));
  main main_7 (.in_1(in_15), .in_2(in_7), .in_3(main_8_out_5), .out_4(out_25), .out_5(main_7_out_5));
  main main_8 (.in_1(in_16), .in_2(in_8), .in_3(in_17), .out_4(out_26), .out_5(main_8_out_5));
endmodule
