// Logisim project Exercicio_01.circ as structural Verilog: 1 circuit, main circuit main
module main (
  input  in_1,
  output out_2,
  output out_3
);

  and and_1 (out_2, in_1, in_1);
  or or_1 (out_3, in_1, in_1);
endmodule
