// Logisim project Exercicio_02.circ as structural Verilog: 1 circuit, main circuit main
module main (
  input  in_1,
  input  in_2,
  output out_3
);

  wire and_1_out, or_1_out;

  and and_1 (and_1_out, in_1, in_1);
  Multiplexer #(.enable("false")) multiplexer_1 (.in0(and_1_out), .in1(or_1_out), .out(out_3), .sel(in_2));
  or or_1 (or_1_out, in_1, in_1);
endmodule
