// Logisim project Exercicio_04.circ as structural Verilog: 1 circuit, main circuit main
module main (
  input  in_1,
  input  [1:0] in_2,
  output out_3
);

  wire nor_1_out, nor_2_out, or_1_out, xor_1_out;

  or or_1 (or_1_out, in_1, in_1);
  nor nor_1 (nor_1_out, in_1, in_1);
  xor xor_1 (xor_1_out, in_1, in_1);
  nor nor_2 (nor_2_out, in_1, in_1);
  Multiplexer #(.select(2), .enable("false")) multiplexer_1 (
    .in0(or_1_out), .in1(nor_1_out), .in2(xor_1_out), .in3(nor_2_out), .out(out_3), .sel(in_2));
endmodule
