// Logisim project Exercicio_06.circ as structural Verilog: 4 circuits, main circuit main
module Complemento_de_2 (
  input  in_1,
  input  in_2,
  input  in_3,
  output out_4,
  output out_5,
  output out_6
);

  wire not_1_out, not_2_out, not_3_out, not_4_out, somador_2_out_5, somador_3_out_5;

  not not_1 (not_1_out, in_1);
  Somador somador_1 (.in_2(not_1_out), .in_3(somador_2_out_5), .in_1(not_4_out), .out_4(out_4));  // open: out_5
  not not_2 (not_2_out, in_2);
  Somador somador_2 (
    .in_2(not_2_out), .in_3(somador_3_out_5), .in_1(not_4_out), .out_4(out_5), .out_5(somador_2_out_5));
  not not_3 (not_3_out, in_3);
  not not_4 (not_4_out, 1'b1);
  Somador somador_3 (.in_2(not_3_out), .in_3(1'b1), .in_1(not_4_out), .out_4(out_6), .out_5(somador_3_out_5));

  // Notes on the sheet:
  //   Two's Complement
endmodule

module main (
  input  in_1,
  input  in_2,
  input  in_3,
  input  in_4,
  input  in_5,
  input  in_6,
  output out_7
);

  wire complemento_de_2_1_out_4, complemento_de_2_1_out_5, complemento_de_2_1_out_6, not_1_out,
       somador_1_out_4, somador_2_out_4, somador_2_out_5, somador_3_out_4, somador_3_out_5;

  Somador somador_1 (
    .in_2(in_1), .in_3(complemento_de_2_1_out_4), .in_1(somador_2_out_5), .out_4(somador_1_out_4));  // open: out_5
  Somador somador_2 (
    .in_2(in_2), .in_3(complemento_de_2_1_out_5), .in_1(somador_3_out_5), .out_4(somador_2_out_4),
    .out_5(somador_2_out_5));
  or or_1 (out_7, somador_1_out_4, somador_2_out_4, somador_3_out_4);
  not not_1 (not_1_out, 1'b1);
  Somador somador_3 (
    .in_2(not_1_out), .in_3(complemento_de_2_1_out_6), .in_1(in_3), .out_4(somador_3_out_4),
    .out_5(somador_3_out_5));
  Complemento_de_2 complemento_de_2_1 (
    .in_1(in_4), .in_2(in_5), .in_3(in_6), .out_4(complemento_de_2_1_out_4),
    .out_5(complemento_de_2_1_out_5), .out_6(complemento_de_2_1_out_6));

  // Notes on the sheet:
  //   Bit de Sinal
  //   Bit de Sinal
  //   0 - Igual/ 1 - Diferente
endmodule

module Meio_Somador (
  input  in_1,
  input  in_2,
  output out_3,
  output out_4
);

  and and_1 (out_3, in_1, in_2);
  xor xor_1 (out_4, in_1, in_2);

  // Notes on the sheet:
  //   Half Adder
endmodule

module Somador (
  input  in_1,
  input  in_2,
  input  in_3,
  output out_4,
  output out_5
);

  wire meio_somador_1_out_3, meio_somador_1_out_4, meio_somador_2_out_3;

  Meio_Somador meio_somador_1 (.in_1(in_3), .in_2(in_2), .out_3(meio_somador_1_out_3), .out_4(meio_somador_1_out_4));
  Meio_Somador meio_somador_2 (.in_1(meio_somador_1_out_4), .in_2(in_1), .out_3(meio_somador_2_out_3), .out_4(out_4));
  or or_1 (out_5, meio_somador_2_out_3, meio_somador_1_out_3);

  // Notes on the sheet:
  //   Full Adder
endmodule
