// Logisim project Exercicio_01.circ as structural Verilog: 3 circuits, main circuit main
module main (
  input  in_1,
  input  in_2,
  output out_3,
  output out_4
);

  xor xor_1 (out_3, in_1, in_2);
  and and_1 (out_4, in_2, in_1);
endmodule

module Full_Adder (
  input  in_1,
  input  in_2,
  input  in_3,
  output out_4,
  output out_5
);

  wire main_1_out_3, main_1_out_4, main_2_out_4;

  main main_1 (.in_1(in_3), .in_2(in_2), .out_3(main_1_out_3), .out_4(main_1_out_4));
  main main_2 (.in_1(main_1_out_3), .in_2(in_1), .out_3(out_4), .out_4(main_2_out_4));
  or or_1 (out_5, main_2_out_4, main_1_out_4);
endmodule

module Full_Adder_4_Bits (
  input  [3:0] in_1,
  input  [3:0] in_2,
  output [4:0] out_3
);

  wire full_adder_2_out_5, full_adder_3_out_5, full_adder_4_out_5, not_1_out;

  Full_Adder full_adder_1 (
    .in_1(full_adder_2_out_5), .in_2(in_2[3]), .in_3(in_1[3]), .out_4(out_3[3]), .out_5(out_3[4]));
  Full_Adder full_adder_2 (
    .in_1(full_adder_3_out_5), .in_2(in_2[2]), .in_3(in_1[2]), .out_4(out_3[2]), .out_5(full_adder_2_out_5));
  Full_Adder full_adder_3 (
    .in_1(full_adder_4_out_5), .in_2(in_2[1]), .in_3(in_1[1]), .out_4(out_3[1]), .out_5(full_adder_3_out_5));
  Full_Adder full_adder_4 (
    .in_1(not_1_out), .in_2(in_2[0]), .in_3(in_1[0]), .out_4(out_3[0]), .out_5(full_adder_4_out_5));
  not not_1 (not_1_out, 1'b1);
endmodule
