// Logisim project Exercicio_02.circ as structural Verilog: 4 circuits, main circuit main
module main (
  input  [3:0] in_1,
  input  [3:0] in_2,
  output [3:0] out_3
);

  wire full_adder_1_out_5, full_adder_3_out_5, full_adder_4_out_5, not_1_out;
  wire [3:0] complemento_de_2_1_out_2;

  Complemento_de_2 complemento_de_2_1 (.in_1(in_1), .out_2(complemento_de_2_1_out_2));
  Full_Adder full_adder_1 (
    .in_1(full_adder_4_out_5), .in_2(complemento_de_2_1_out_2[2]), .in_3(in_2[2]), .out_4(out_3[2]),
    .out_5(full_adder_1_out_5));
  Full_Adder full_adder_2 (
    .in_1(full_adder_1_out_5), .in_2(complemento_de_2_1_out_2[3]), .in_3(in_2[3]), .out_4(out_3[3]));  // open: out_5
  Full_Adder full_adder_3 (
    .in_1(not_1_out), .in_2(complemento_de_2_1_out_2[0]), .in_3(in_2[0]), .out_4(out_3[0]),
    .out_5(full_adder_3_out_5));
  Full_Adder full_adder_4 (
    .in_1(full_adder_3_out_5), .in_2(complemento_de_2_1_out_2[1]), .in_3(in_2[1]), .out_4(out_3[1]),
    .out_5(full_adder_4_out_5));
  not not_1 (not_1_out, 1'b1);
endmodule

module Half_Adder (
  input  in_1,
  input  in_2,
  output out_3,
  output out_4
);

  xor xor_1 (out_3, in_2, in_1);
  and and_1 (out_4, in_1, in_2);
endmodule

module Full_Adder (
  input  in_1,
  input  in_2,
  input  in_3,
  output out_4,
  output out_5
);

  wire half_adder_1_out_3, half_adder_1_out_4, half_adder_2_out_4;

  Half_Adder half_adder_1 (.in_1(in_3), .in_2(in_2), .out_3(half_adder_1_out_3), .out_4(half_adder_1_out_4));
  Half_Adder half_adder_2 (.in_1(half_adder_1_out_3), .in_2(in_1), .out_3(out_4), .out_4(half_adder_2_out_4));
  or or_1 (out_5, half_adder_2_out_4, half_adder_1_out_4);
endmodule

module Complemento_de_2 (
  input  [3:0] in_1,
  output [3:0] out_2
);

  wire half_adder_2_out_4, half_adder_3_out_4, half_adder_4_out_4, not_1_out, not_2_out, not_3_out, not_4_out;

  Half_Adder half_adder_1 (.in_1(not_3_out), .in_2(half_adder_2_out_4), .out_3(out_2[3]));  // open: out_4
  Half_Adder half_adder_2 (.in_1(not_2_out), .in_2(half_adder_3_out_4), .out_3(out_2[2]), .out_4(half_adder_2_out_4));
  not not_1 (not_1_out, in_1[1]);
  not not_2 (not_2_out, in_1[2]);
  not not_3 (not_3_out, in_1[3]);
  not not_4 (not_4_out, in_1[0]);
  Half_Adder half_adder_3 (.in_1(not_1_out), .in_2(half_adder_4_out_4), .out_3(out_2[1]), .out_4(half_adder_3_out_4));
  Half_Adder half_adder_4 (.in_1(not_4_out), .in_2(1'b1), .out_3(out_2[0]), .out_4(half_adder_4_out_4));
endmodule
