// Logisim project Exercicio_03.circ as structural Verilog: 2 circuits, main circuit main
module main (
  input  [3:0] in_1,
  input  [3:0] in_2,
  output out_3
);

  wire and_1_out, and_2_out, igualdade_1_out_3, igualdade_2_out_3, igualdade_3_out_3, igualdade_4_out_3,
       not_1_out, not_2_out, not_3_out, not_4_out;

  Igualdade igualdade_1 (.in_1(in_2[3]), .in_2(in_1[3]), .out_3(igualdade_1_out_3));
  Igualdade igualdade_2 (.in_1(in_2[2]), .in_2(in_1[2]), .out_3(igualdade_2_out_3));
  and and_1 (and_1_out, igualdade_1_out_3, igualdade_2_out_3, igualdade_3_out_3, igualdade_4_out_3);
  Igualdade igualdade_3 (.in_1(in_2[1]), .in_2(in_1[1]), .out_3(igualdade_3_out_3));
  Igualdade igualdade_4 (.in_1(in_2[0]), .in_2(in_1[0]), .out_3(igualdade_4_out_3));
  not not_1 (not_1_out, igualdade_1_out_3);
  not not_2 (not_2_out, igualdade_3_out_3);
  not not_3 (not_3_out, igualdade_2_out_3);
  and and_2 (and_2_out, not_1_out, not_3_out, not_2_out, not_4_out);
  or or_1 (out_3, and_1_out, and_2_out);
  not not_4 (not_4_out, igualdade_4_out_3);
endmodule

module Igualdade (
  input  in_1,
  input  in_2,
  output out_3
);

  xnor xnor_1 (out_3, in_1, in_2);
endmodule
