// Logisim project Exercicio_04.circ as structural Verilog: 2 circuits, main circuit main
module main (
  input  [3:0] in_1,
  input  [3:0] in_2,
  output out_3
);

  wire \diferença_1_out_3 , \diferença_2_out_3 , \diferença_3_out_3 , \diferença_4_out_3 , not_1_out,
       not_2_out, not_3_out, not_4_out, or_1_out, or_2_out;

  \Diferença  \diferença_1  (.in_1(in_2[3]), .in_2(in_1[3]), .out_3(\diferença_1_out_3 ));
  \Diferença  \diferença_2  (.in_1(in_2[2]), .in_2(in_1[2]), .out_3(\diferença_2_out_3 ));
  or or_1 (or_1_out, \diferença_1_out_3 , \diferença_2_out_3 , \diferença_4_out_3 , \diferença_3_out_3 );
  \Diferença  \diferença_3  (.in_1(in_2[0]), .in_2(in_1[0]), .out_3(\diferença_3_out_3 ));
  \Diferença  \diferença_4  (.in_1(in_2[1]), .in_2(in_1[1]), .out_3(\diferença_4_out_3 ));
  not not_1 (not_1_out, \diferença_1_out_3 );
  not not_2 (not_2_out, \diferença_4_out_3 );
  not not_3 (not_3_out, \diferença_2_out_3 );
  or or_2 (or_2_out, not_1_out, not_3_out, not_2_out, not_4_out);
  and and_1 (out_3, or_1_out, or_2_out);
  not not_4 (not_4_out, \diferença_3_out_3 );
endmodule

module \Diferença  (
  input  in_1,
  input  in_2,
  output out_3
);

  xor xor_1 (out_3, in_1, in_2);
endmodule
