// Logisim project Exercicio_07_Extra.circ as structural Verilog: 5 circuits, main circuit main
module main (
  input  [3:0] in_1,
  input  [3:0] in_2,
  input  in_3,
  output out_4
);

  wire desigualdade_4_bits_1_out_3, igualdade_de_4_bits_1_out_3;

  Igualdade_de_4_bits igualdade_de_4_bits_1 (.in_1(in_2), .out_3(igualdade_de_4_bits_1_out_3), .in_2(in_1));
  Desigualdade_4_bits desigualdade_4_bits_1 (.in_2(in_2), .out_3(desigualdade_4_bits_1_out_3), .in_1(in_1));
  Multiplexer #(.enable("false")) multiplexer_1 (
    .in0(igualdade_de_4_bits_1_out_3), .in1(desigualdade_4_bits_1_out_3), .out(out_4), .sel(in_3));
endmodule

module Igualdade (
  input  in_1,
  input  in_2,
  output out_3
);

  xnor xnor_1 (out_3, in_1, in_2);
endmodule

module Desigualdade (
  input  in_1,
  input  in_2,
  output out_3
);

  xor xor_1 (out_3, in_1, in_2);
endmodule

module Igualdade_de_4_bits (
  input  [3:0] in_1,
  input  [3:0] in_2,
  output out_3
);

  wire and_1_out, and_2_out, igualdade_1_out_3, igualdade_2_out_3, igualdade_3_out_3, igualdade_4_out_3,
       not_1_out, not_2_out, not_3_out, not_4_out;

  Igualdade igualdade_1 (.in_1(in_2[3]), .in_2(in_1[3]), .out_3(igualdade_1_out_3));
  Igualdade igualdade_2 (.in_1(in_2[1]), .in_2(in_1[1]), .out_3(igualdade_2_out_3));
  Igualdade igualdade_3 (.in_1(in_2[2]), .in_2(in_1[2]), .out_3(igualdade_3_out_3));
  not not_1 (not_1_out, igualdade_1_out_3);
  and and_1 (and_1_out, igualdade_1_out_3, igualdade_3_out_3, igualdade_2_out_3, igualdade_4_out_3);
  or or_1 (out_3, and_1_out, and_2_out);
  Igualdade igualdade_4 (.in_1(in_2[0]), .in_2(in_1[0]), .out_3(igualdade_4_out_3));
  not not_2 (not_2_out, igualdade_4_out_3);
  not not_3 (not_3_out, igualdade_2_out_3);
  not not_4 (not_4_out, igualdade_3_out_3);
  and and_2 (and_2_out, not_1_out, not_4_out, not_3_out, not_2_out);
endmodule

module Desigualdade_4_bits (
  input  [3:0] in_1,
  input  [3:0] in_2,
  output out_3
);

  wire desigualdade_1_out_3, desigualdade_2_out_3, desigualdade_3_out_3, desigualdade_4_out_3, not_1_out,
       not_2_out, not_3_out, not_4_out, or_1_out, or_2_out;

  Desigualdade desigualdade_1 (.in_1(in_1[2]), .in_2(in_2[2]), .out_3(desigualdade_1_out_3));
  Desigualdade desigualdade_2 (.in_1(in_1[3]), .in_2(in_2[3]), .out_3(desigualdade_2_out_3));
  or or_1 (or_1_out, desigualdade_2_out_3, desigualdade_1_out_3, desigualdade_3_out_3, desigualdade_4_out_3);
  Desigualdade desigualdade_3 (.in_1(in_1[1]), .in_2(in_2[1]), .out_3(desigualdade_3_out_3));
  not not_1 (not_1_out, desigualdade_1_out_3);
  not not_2 (not_2_out, desigualdade_2_out_3);
  not not_3 (not_3_out, desigualdade_3_out_3);
  or or_2 (or_2_out, not_2_out, not_1_out, not_3_out, not_4_out);
  and and_1 (out_3, or_1_out, or_2_out);
  Desigualdade desigualdade_4 (.in_1(in_1[0]), .in_2(in_2[0]), .out_3(desigualdade_4_out_3));
  not not_4 (not_4_out, desigualdade_4_out_3);
endmodule
