// Logisim project Moore_1101.circ as structural Verilog: 1 circuit, main circuit main
module main (
  input  in_1,
  input  in_2,
  output out_3
);

  wire clock_1_out, d_ff_1_q, d_ff_1_qn, d_ff_2_q, d_ff_2_qn, d_ff_3_q, d_ff_3_qn, d_ff_4_q, d_ff_4_qn,
       not_1_out;

  Clock clock_1 (.out(clock_1_out));
  // Probe on d_ff_1_q
  D_Flip_Flop d_ff_1 (.clk(clock_1_out), .D(in_1), .Q(d_ff_1_q), .Qn(d_ff_1_qn), .reset(in_2));  // open: preset
  // Probe on d_ff_1_qn
  // Probe on d_ff_2_q
  D_Flip_Flop d_ff_2 (.clk(clock_1_out), .D(d_ff_1_q), .Q(d_ff_2_q), .Qn(d_ff_2_qn), .reset(in_2));  // open: preset
  // Probe on d_ff_2_qn
  // Probe on d_ff_3_q
  D_Flip_Flop d_ff_3 (.clk(clock_1_out), .D(d_ff_2_q), .Q(d_ff_3_q), .Qn(d_ff_3_qn), .reset(in_2));  // open: preset
  // Probe on d_ff_3_qn
  // Probe on d_ff_4_q
  D_Flip_Flop d_ff_4 (.clk(clock_1_out), .D(d_ff_3_q), .Q(d_ff_4_q), .Qn(d_ff_4_qn), .reset(in_2));  // open: preset
  // Probe on d_ff_4_qn
  not not_1 (not_1_out, d_ff_3_q);
  D_Flip_Flop d_ff_5 (.clk(clock_1_out), .D(out_3), .reset(in_2));  // open: Q, Qn, preset
  and and_1 (out_3, d_ff_1_q, d_ff_2_q, not_1_out, d_ff_4_q);
endmodule
