// Logisim project Exemplo_1101.circ as structural Verilog: 3 circuits, main circuit main
module main (
  input  Input,
  input  Clear,
  input  in_3,
  output out_4,
  output out_5
);

  wire clock_1_out, mearly_1_out_4, moore_1_out_4, moore_1_out_5;

  Clock clock_1 (.out(clock_1_out));
  Mearly mearly_1 (.in_1(clock_1_out), .in_2(Input), .in_3(Clear), .out_4(mearly_1_out_4));
  Multiplexer #(.enable("false")) multiplexer_1 (.in0(mearly_1_out_4), .in1(moore_1_out_4), .out(out_4), .sel(in_3));
  Moore moore_1 (.in_1(clock_1_out), .in_2(Input), .in_3(Clear), .out_4(moore_1_out_4), .out_5(moore_1_out_5));
  and and_1 (out_5, in_3, moore_1_out_5);

  // Notes on the sheet:
  //   Moore Machine
  //   Mearly Machine
endmodule

module Mearly (
  input  in_1,
  input  in_2,
  input  in_3,
  output out_4
);

  wire d_ff_1_q, d_ff_1_qn, d_ff_2_q, d_ff_2_qn, d_ff_3_q, d_ff_3_qn, d_ff_4_q, d_ff_4_qn, not_1_out;

  // Probe on d_ff_1_q
  D_Flip_Flop d_ff_1 (.clk(in_1), .D(in_2), .Q(d_ff_1_q), .Qn(d_ff_1_qn), .reset(in_3));  // open: preset
  // Probe on d_ff_1_qn
  // Probe on d_ff_2_q
  D_Flip_Flop d_ff_2 (.clk(in_1), .D(d_ff_1_q), .Q(d_ff_2_q), .Qn(d_ff_2_qn), .reset(in_3));  // open: preset
  // Probe on d_ff_2_qn
  // Probe on d_ff_3_q
  D_Flip_Flop d_ff_3 (.clk(in_1), .D(d_ff_2_q), .Q(d_ff_3_q), .Qn(d_ff_3_qn), .reset(in_3));  // open: preset
  // Probe on d_ff_3_qn
  // Probe on d_ff_4_q
  D_Flip_Flop d_ff_4 (.clk(in_1), .D(d_ff_3_q), .Q(d_ff_4_q), .Qn(d_ff_4_qn), .reset(in_3));  // open: preset
  // Probe on d_ff_4_qn
  and and_1 (out_4, d_ff_1_q, d_ff_2_q, not_1_out, d_ff_4_q);
  not not_1 (not_1_out, d_ff_3_q);
endmodule

module Moore (
  input  in_1,
  input  in_2,
  input  in_3,
  output out_4,
  output out_5
);

  wire d_ff_1_q, d_ff_1_qn, d_ff_2_q, d_ff_2_qn, d_ff_3_q, d_ff_3_qn, d_ff_4_q, d_ff_4_qn, not_1_out;

  // Probe on d_ff_1_q
  D_Flip_Flop d_ff_1 (.clk(in_1), .D(in_2), .Q(d_ff_1_q), .Qn(d_ff_1_qn), .reset(in_3));  // open: preset
  // Probe on d_ff_1_qn
  // Probe on d_ff_2_q
  D_Flip_Flop d_ff_2 (.clk(in_1), .D(d_ff_1_q), .Q(d_ff_2_q), .Qn(d_ff_2_qn), .reset(in_3));  // open: preset
  // Probe on d_ff_2_qn
  // Probe on d_ff_3_q
  D_Flip_Flop d_ff_3 (.clk(in_1), .D(d_ff_2_q), .Q(d_ff_3_q), .Qn(d_ff_3_qn), .reset(in_3));  // open: preset
  // Probe on d_ff_3_qn
  // Probe on d_ff_4_q
  D_Flip_Flop d_ff_4 (.clk(in_1), .D(d_ff_3_q), .Q(d_ff_4_q), .Qn(d_ff_4_qn), .reset(in_3));  // open: preset
  // Probe on d_ff_4_qn
  not not_1 (not_1_out, d_ff_3_q);
  and and_1 (out_5, d_ff_1_q, d_ff_2_q, not_1_out, d_ff_4_q);
  D_Flip_Flop d_ff_5 (.clk(in_1), .D(out_5), .Q(out_4), .reset(in_3));  // open: Qn, preset
endmodule
