// Logisim project Exemplo_1104.circ as structural Verilog: 2 circuits, main circuit main
module main (
  input  in_1,
  input  in_2,
  output out_3
);

  wire and_1_out, clock_1_out, d_ff_1_q, d_ff_1_qn, d_ff_2_q, d_ff_2_qn, d_ff_3_q, d_ff_3_qn, not_1_out,
       not_2_out, not_3_out, not_4_out, not_5_out, not_6_out, not_7_out, not_8_out;
  wire [7:0] contator_1_out_4;

  Clock clock_1 (.out(clock_1_out));
  // Probe on d_ff_1_q
  D_Flip_Flop d_ff_1 (.clk(clock_1_out), .D(in_1), .Q(d_ff_1_q), .Qn(d_ff_1_qn), .reset(in_2));  // open: preset
  // Probe on d_ff_1_qn
  // Probe on d_ff_2_q
  D_Flip_Flop d_ff_2 (.clk(clock_1_out), .D(d_ff_1_q), .Q(d_ff_2_q), .Qn(d_ff_2_qn), .reset(in_2));  // open: preset
  // Probe on d_ff_2_qn
  // Probe on d_ff_3_q
  D_Flip_Flop d_ff_3 (.clk(clock_1_out), .D(d_ff_2_q), .Q(d_ff_3_q), .Qn(d_ff_3_qn), .reset(in_2));  // open: preset
  // Probe on d_ff_3_qn
  not not_1 (not_1_out, d_ff_2_q);
  Contator contator_1 (
    .in_2(and_1_out), .in_3(in_2), .in_1(clock_1_out),
    .out_4({contator_1_out_4[7:5], contator_1_out_4[5], contator_1_out_4[3:0]}));
  and and_1 (and_1_out, d_ff_1_q, not_1_out, d_ff_3_q);
  not not_2 (not_2_out, contator_1_out_4[1]);
  not not_3 (not_3_out, contator_1_out_4[2]);
  not not_4 (not_4_out, contator_1_out_4[3]);
  not not_5 (not_5_out, contator_1_out_4[5]);
  not not_6 (not_6_out, contator_1_out_4[5]);
  not not_7 (not_7_out, contator_1_out_4[6]);
  not not_8 (not_8_out, contator_1_out_4[7]);
  and and_2 (out_3, contator_1_out_4[0], not_2_out, not_3_out, not_4_out, not_5_out, not_6_out, not_7_out, not_8_out);
endmodule

module Contator (
  input  in_1,
  input  in_2,
  input  in_3,
  output [7:0] out_4
);

  wire j_k_ff_1_qn, j_k_ff_2_qn, j_k_ff_3_qn, j_k_ff_4_qn, j_k_ff_5_qn, j_k_ff_6_qn, j_k_ff_7_qn;

  J_K_Flip_Flop j_k_ff_1 (
    .J(in_2), .clk(in_1), .K(in_2), .Q(out_4[0]), .Qn(j_k_ff_1_qn), .reset(in_3));  // open: preset
  J_K_Flip_Flop j_k_ff_2 (
    .J(in_2), .clk(j_k_ff_1_qn), .K(in_2), .Q(out_4[1]), .Qn(j_k_ff_2_qn), .reset(in_3));  // open: preset
  J_K_Flip_Flop j_k_ff_3 (
    .J(in_2), .clk(j_k_ff_2_qn), .K(in_2), .Q(out_4[2]), .Qn(j_k_ff_3_qn), .reset(in_3));  // open: preset
  J_K_Flip_Flop j_k_ff_4 (
    .J(in_2), .clk(j_k_ff_3_qn), .K(in_2), .Q(out_4[3]), .Qn(j_k_ff_4_qn), .reset(in_3));  // open: preset
  J_K_Flip_Flop j_k_ff_5 (
    .J(in_2), .clk(j_k_ff_4_qn), .K(in_2), .Q(out_4[4]), .Qn(j_k_ff_5_qn), .reset(in_3));  // open: preset
  J_K_Flip_Flop j_k_ff_6 (
    .J(in_2), .clk(j_k_ff_5_qn), .K(in_2), .Q(out_4[5]), .Qn(j_k_ff_6_qn), .reset(in_3));  // open: preset
  J_K_Flip_Flop j_k_ff_7 (
    .J(in_2), .clk(j_k_ff_6_qn), .K(in_2), .Q(out_4[6]), .Qn(j_k_ff_7_qn), .reset(in_3));  // open: preset
  J_K_Flip_Flop j_k_ff_8 (.clk(j_k_ff_7_qn), .K(in_2), .Q(out_4[7]), .reset(in_3));  // open: J, Qn, preset
endmodule
