// Logisim project Exercicio1.circ as structural Verilog: 3 circuits, main circuit main
module main (
  input  \Endereço ,
  input  R___0___W___1,
  input  Clock,
  input  [3:0] Entrada,
  input  Clear,
  output [3:0] \Saída 
);

  _1x4 u_1x4_1 (.in_1(\Endereço ), .in_2(R___0___W___1), .in_3(Clock), .in_4(Entrada), .in_5(Clear), .out_6(\Saída ));
endmodule

module Mem_4bits (
  input  in_1,
  input  in_2,
  input  in_3,
  input  in_4,
  input  in_5,
  output out_6
);

  wire and_1_out, d_ff_1_q, not_1_out;

  not not_1 (not_1_out, in_2);
  and and_1 (and_1_out, in_1, in_2, in_3);
  D_Flip_Flop d_ff_1 (.clk(and_1_out), .D(in_4), .Q(d_ff_1_q), .reset(in_5));  // open: Qn, preset
  and and_2 (out_6, in_1, not_1_out, d_ff_1_q);
endmodule

module _1x4 (
  input  in_1,
  input  in_2,
  input  in_3,
  input  [3:0] in_4,
  input  in_5,
  output [3:0] out_6
);

  Mem_4bits mem_4bits_1 (.in_1(in_1), .in_2(in_2), .in_3(in_3), .in_4(in_4[2]), .in_5(in_5), .out_6(out_6[2]));
  Mem_4bits mem_4bits_2 (.in_1(in_1), .in_2(in_2), .in_3(in_3), .in_4(in_4[3]), .in_5(in_5), .out_6(out_6[3]));
  Mem_4bits mem_4bits_3 (.in_1(in_1), .in_2(in_2), .in_3(in_3), .in_4(in_4[1]), .in_5(in_5), .out_6(out_6[1]));
  Mem_4bits mem_4bits_4 (.in_1(in_1), .in_2(in_2), .in_3(in_3), .in_4(in_4[0]), .in_5(in_5), .out_6(out_6[0]));
endmodule
