// Logisim project Exercicio4.circ as structural Verilog: 5 circuits, main circuit main
module main (
  input  R___0___w___1,
  input  [7:0] Entrada,
  input  [1:0] \Endereço ,
  input  Clear,
  output [7:0] \Saída 
);

  wire Clock_out, demultiplexer_1_out0, demultiplexer_1_out1, demultiplexer_1_out2, demultiplexer_1_out3;
  wire [7:0] n1x8_1_out_6, n1x8_2_out_6, n1x8_3_out_6, n1x8_4_out_6;

  Clock Clock (.out(Clock_out));
  Demultiplexer #(.select(2), .enable("false")) demultiplexer_1 (
    .out0(demultiplexer_1_out0), .out1(demultiplexer_1_out1), .out2(demultiplexer_1_out2),
    .out3(demultiplexer_1_out3), .in(1'b1), .sel(\Endereço ));
  _1x8 u_1x8_1 (
    .in_1(demultiplexer_1_out0), .in_2(R___0___w___1), .in_3(Clock_out), .in_4(Entrada), .in_5(Clear),
    .out_6(n1x8_1_out_6));
  _1x8 u_1x8_2 (
    .in_1(demultiplexer_1_out1), .in_2(R___0___w___1), .in_3(Clock_out), .in_4(Entrada), .in_5(Clear),
    .out_6(n1x8_2_out_6));
  _1x8 u_1x8_3 (
    .in_1(demultiplexer_1_out2), .in_2(R___0___w___1), .in_3(Clock_out), .in_4(Entrada), .in_5(Clear),
    .out_6(n1x8_3_out_6));
  _1x8 u_1x8_4 (
    .in_1(demultiplexer_1_out3), .in_2(R___0___w___1), .in_3(Clock_out), .in_4(Entrada), .in_5(Clear),
    .out_6(n1x8_4_out_6));
  assign \Saída  = n1x8_1_out_6 | n1x8_2_out_6 | n1x8_3_out_6 | n1x8_4_out_6;  // OR_Gate or_1, 8 bits wide
endmodule

module _1x1 (
  input  in_1,
  input  in_2,
  input  in_3,
  input  in_4,
  input  in_5,
  output out_6
);

  wire and_1_out, d_ff_1_q, not_1_out;

  not not_1 (not_1_out, in_2);
  and and_1 (and_1_out, in_1, in_2, in_3);
  D_Flip_Flop d_ff_1 (.clk(and_1_out), .D(in_4), .Q(d_ff_1_q), .reset(in_5));  // open: Qn, preset
  and and_2 (out_6, in_1, not_1_out, d_ff_1_q);
endmodule

module _1x2 (
  input  in_1,
  input  in_2,
  input  in_3,
  input  [1:0] in_4,
  input  in_5,
  output [1:0] out_6
);

  _1x1 u_1x1_1 (.in_1(in_1), .in_2(in_2), .in_3(in_3), .in_4(in_4[1]), .in_5(in_5), .out_6(out_6[1]));
  _1x1 u_1x1_2 (.in_1(in_1), .in_2(in_2), .in_3(in_3), .in_4(in_4[0]), .in_5(in_5), .out_6(out_6[0]));
endmodule

module _1x4 (
  input  in_1,
  input  in_2,
  input  in_3,
  input  [3:0] in_4,
  input  in_5,
  output [3:0] out_6
);

  _1x2 u_1x2_1 (.in_1(in_1), .in_2(in_2), .in_3(in_3), .in_4(in_4[3:2]), .in_5(in_5), .out_6(out_6[3:2]));
  _1x2 u_1x2_2 (.in_1(in_1), .in_2(in_2), .in_3(in_3), .in_4(in_4[1:0]), .in_5(in_5), .out_6(out_6[1:0]));
endmodule

module _1x8 (
  input  in_1,
  input  in_2,
  input  in_3,
  input  [7:0] in_4,
  input  in_5,
  output [7:0] out_6
);

  _1x4 u_1x4_1 (.in_1(in_1), .in_2(in_2), .in_3(in_3), .in_4(in_4[7:4]), .in_5(in_5), .out_6(out_6[7:4]));
  _1x4 u_1x4_2 (.in_1(in_1), .in_2(in_2), .in_3(in_3), .in_4(in_4[3:0]), .in_5(in_5), .out_6(out_6[3:0]));
endmodule
