// Logisim project Exercicio5.circ as structural Verilog: 6 circuits, main circuit main
module _1x1 (
  input  in_1,
  input  in_2,
  input  in_3,
  input  in_4,
  input  in_5,
  output out_6
);

  wire and_1_out, d_ff_1_q, not_1_out;

  not not_1 (not_1_out, in_2);
  and and_1 (and_1_out, in_1, in_2, in_3);
  D_Flip_Flop d_ff_1 (.clk(and_1_out), .D(in_4), .Q(d_ff_1_q), .reset(in_5));  // open: Qn, preset
  and and_2 (out_6, in_1, not_1_out, d_ff_1_q);
endmodule

module main (
  input  R___0___W___1,
  input  [7:0] Entrada,
  input  [1:0] Indice,
  input  Chave,
  input  Clear,
  output [7:0] \Saída 
);

  wire and_1_out, and_2_out, Clock_out, not_1_out;
  wire [1:0] demultiplexer_1_out0, demultiplexer_1_out1;
  wire [7:0] n4x8_1_out_6, n4x8_2_out_6;

  Clock Clock (.out(Clock_out));
  not not_1 (not_1_out, Chave);
  and and_1 (and_1_out, not_1_out, Clock_out);
  and and_2 (and_2_out, Chave, Clock_out);
  Demultiplexer #(.width(2), .enable("false")) demultiplexer_1 (
    .out0(demultiplexer_1_out0), .out1(demultiplexer_1_out1), .in(Indice), .sel(Chave));
  _4x8 u_4x8_1 (
    .in_1(R___0___W___1), .in_2(and_1_out), .in_3(Entrada), .in_4(demultiplexer_1_out0), .in_5(Clear),
    .out_6(n4x8_1_out_6));
  _4x8 u_4x8_2 (
    .in_1(R___0___W___1), .in_2(and_2_out), .in_3(Entrada), .in_4(demultiplexer_1_out1), .in_5(Clear),
    .out_6(n4x8_2_out_6));
  Multiplexer #(.width(8), .enable("false")) multiplexer_1 (
    .in0(n4x8_1_out_6), .in1(n4x8_2_out_6), .out(\Saída ), .sel(Chave));
endmodule

module _1x2 (
  input  in_1,
  input  in_2,
  input  in_3,
  input  [1:0] in_4,
  input  in_5,
  output [1:0] out_6
);

  _1x1 u_1x1_1 (.in_1(in_1), .in_2(in_2), .in_3(in_3), .in_4(in_4[1]), .in_5(in_5), .out_6(out_6[1]));
  _1x1 u_1x1_2 (.in_1(in_1), .in_2(in_2), .in_3(in_3), .in_4(in_4[0]), .in_5(in_5), .out_6(out_6[0]));
endmodule

module _1x4 (
  input  in_1,
  input  in_2,
  input  in_3,
  input  [3:0] in_4,
  input  in_5,
  output [3:0] out_6
);

  _1x2 u_1x2_1 (.in_1(in_1), .in_2(in_2), .in_3(in_3), .in_4(in_4[3:2]), .in_5(in_5), .out_6(out_6[3:2]));
  _1x2 u_1x2_2 (.in_1(in_1), .in_2(in_2), .in_3(in_3), .in_4(in_4[1:0]), .in_5(in_5), .out_6(out_6[1:0]));
endmodule

module _1x8 (
  input  in_1,
  input  in_2,
  input  in_3,
  input  [7:0] in_4,
  input  in_5,
  output [7:0] out_6
);

  _1x4 u_1x4_1 (.in_1(in_1), .in_2(in_2), .in_3(in_3), .in_4(in_4[7:4]), .in_5(in_5), .out_6(out_6[7:4]));
  _1x4 u_1x4_2 (.in_1(in_1), .in_2(in_2), .in_3(in_3), .in_4(in_4[3:0]), .in_5(in_5), .out_6(out_6[3:0]));
endmodule

module _4x8 (
  input  in_1,
  input  in_2,
  input  [7:0] in_3,
  input  [1:0] in_4,
  input  in_5,
  output [7:0] out_6
);

  wire demultiplexer_1_out0, demultiplexer_1_out1, demultiplexer_1_out2, demultiplexer_1_out3;
  wire [7:0] n1x8_1_out_6, n1x8_2_out_6, n1x8_3_out_6, n1x8_4_out_6;

  Demultiplexer #(.select(2), .enable("false")) demultiplexer_1 (
    .out0(demultiplexer_1_out0), .out1(demultiplexer_1_out1), .out2(demultiplexer_1_out2),
    .out3(demultiplexer_1_out3), .in(1'b1), .sel(in_4));
  _1x8 u_1x8_1 (.in_1(demultiplexer_1_out0), .in_2(in_1), .in_3(in_2), .in_4(in_3), .in_5(in_5), .out_6(n1x8_1_out_6));
  _1x8 u_1x8_2 (.in_1(demultiplexer_1_out1), .in_2(in_1), .in_3(in_2), .in_4(in_3), .in_5(in_5), .out_6(n1x8_2_out_6));
  _1x8 u_1x8_3 (.in_1(demultiplexer_1_out2), .in_2(in_1), .in_3(in_2), .in_4(in_3), .in_5(in_5), .out_6(n1x8_3_out_6));
  _1x8 u_1x8_4 (.in_1(demultiplexer_1_out3), .in_2(in_1), .in_3(in_2), .in_4(in_3), .in_5(in_5), .out_6(n1x8_4_out_6));
  assign out_6 = n1x8_1_out_6 | n1x8_2_out_6 | n1x8_3_out_6 | n1x8_4_out_6;  // OR_Gate or_1, 8 bits wide
endmodule
