// Logisim project Exercicio1.circ as structural Verilog: 2 circuits, main circuit main
module main (
  input  in_1,
  input  in_2,
  input  in_3,
  output [5:0] out_4,
  output [5:0] out_5
);

  wire clock_1_out;

  Clock clock_1 (.out(clock_1_out));
  Registrador registrador_1 (.in_1(clock_1_out), .in_2(in_1), .in_3(in_2), .in_4(in_3), .out_5(out_4), .out_6(out_5));
endmodule

module Registrador (
  input  in_1,
  input  in_2,
  input  in_3,
  input  in_4,
  output [5:0] out_5,
  output [5:0] out_6
);

  D_Flip_Flop d_ff_1 (.clk(in_1), .D(out_5[4]), .Q(out_5[5]), .Qn(out_6[5]), .preset(in_2), .reset(in_4));
  D_Flip_Flop d_ff_2 (.clk(in_1), .D(out_5[3]), .Q(out_5[4]), .Qn(out_6[4]), .preset(in_2), .reset(in_4));
  D_Flip_Flop d_ff_3 (.clk(in_1), .D(out_5[2]), .Q(out_5[3]), .Qn(out_6[3]), .preset(in_2), .reset(in_4));
  D_Flip_Flop d_ff_4 (.clk(in_1), .D(out_5[1]), .Q(out_5[2]), .Qn(out_6[2]), .preset(in_2), .reset(in_4));
  D_Flip_Flop d_ff_5 (.clk(in_1), .D(out_5[0]), .Q(out_5[1]), .Qn(out_6[1]), .preset(in_2), .reset(in_4));
  D_Flip_Flop d_ff_6 (.clk(in_1), .D(in_3), .Q(out_5[0]), .Qn(out_6[0]), .preset(in_2), .reset(in_4));
endmodule
