// Logisim project Exercicio5.circ as structural Verilog: 1 circuit, main circuit main
module main (
  input  in_1,
  input  in_2,
  input  in_3,
  input  in_4,
  input  in_5,
  input  in_6,
  input  in_7,
  input  in_8
);

  wire and_1_out, and_2_out, and_3_out, and_4_out, and_5_out, and_6_out, clock_1_out, d_ff_1_q, d_ff_1_qn,
       d_ff_2_q, d_ff_2_qn, d_ff_3_q, d_ff_3_qn, d_ff_4_q, d_ff_4_qn, d_ff_5_q, d_ff_5_qn, d_ff_6_q,
       d_ff_6_qn;

  Clock clock_1 (.out(clock_1_out));
  // Probe on d_ff_1_q
  D_Flip_Flop #(.Pre_Clr_Positions("LEGACY")) d_ff_1 (
    .clk(clock_1_out), .D(1'b0), .Q(d_ff_1_q), .Qn(d_ff_1_qn), .preset(and_1_out), .reset(in_1));
  and and_1 (and_1_out, in_2, in_3);
  // Probe on d_ff_1_qn
  // Probe on d_ff_2_q
  D_Flip_Flop #(.Pre_Clr_Positions("LEGACY")) d_ff_2 (
    .clk(clock_1_out), .D(d_ff_1_q), .Q(d_ff_2_q), .Qn(d_ff_2_qn), .preset(and_2_out), .reset(in_1));
  // Probe on d_ff_2_qn
  and and_2 (and_2_out, in_2, in_4);
  // Probe on d_ff_3_q
  D_Flip_Flop #(.Pre_Clr_Positions("LEGACY")) d_ff_3 (
    .clk(clock_1_out), .D(d_ff_2_q), .Q(d_ff_3_q), .Qn(d_ff_3_qn), .preset(and_3_out), .reset(in_1));
  and and_3 (and_3_out, in_2, in_5);
  // Probe on d_ff_3_qn
  // Probe on d_ff_4_q
  D_Flip_Flop #(.Pre_Clr_Positions("LEGACY")) d_ff_4 (
    .clk(clock_1_out), .D(d_ff_3_q), .Q(d_ff_4_q), .Qn(d_ff_4_qn), .preset(and_4_out), .reset(in_1));
  and and_4 (and_4_out, in_2, in_6);
  // Probe on d_ff_4_qn
  // Probe on d_ff_5_q
  D_Flip_Flop #(.Pre_Clr_Positions("LEGACY")) d_ff_5 (
    .clk(clock_1_out), .D(d_ff_4_q), .Q(d_ff_5_q), .Qn(d_ff_5_qn), .preset(and_5_out), .reset(in_1));
  // Probe on d_ff_5_qn
  and and_5 (and_5_out, in_2, in_7);
  // Probe on d_ff_6_q
  D_Flip_Flop #(.Pre_Clr_Positions("LEGACY")) d_ff_6 (
    .clk(clock_1_out), .D(d_ff_5_q), .Q(d_ff_6_q), .Qn(d_ff_6_qn), .preset(and_6_out), .reset(in_1));
  // Probe on d_ff_6_qn
  and and_6 (and_6_out, in_2, in_8);
endmodule
