// Logisim project Exercicio6.circ as structural Verilog: 1 circuit, main circuit main
module main (
  input  in_1,
  input  in_2,
  input  in_3,
  input  in_4
);

  wire d_ff_1_q, d_ff_1_qn, d_ff_2_q, d_ff_2_qn, d_ff_3_q, d_ff_3_qn, d_ff_4_q, d_ff_4_qn, d_ff_5_q,
       d_ff_5_qn, d_ff_6_q, d_ff_6_qn, or_1_out;

  or or_1 (or_1_out, d_ff_6_q, in_3);
  // Probe on d_ff_1_q
  D_Flip_Flop d_ff_1 (.clk(in_1), .D(or_1_out), .Q(d_ff_1_q), .Qn(d_ff_1_qn), .preset(in_2), .reset(in_4));
  // Probe on d_ff_1_qn
  // Probe on d_ff_2_q
  D_Flip_Flop d_ff_2 (.clk(in_1), .D(d_ff_1_q), .Q(d_ff_2_q), .Qn(d_ff_2_qn), .preset(in_2), .reset(in_4));
  // Probe on d_ff_2_qn
  // Probe on d_ff_3_q
  D_Flip_Flop d_ff_3 (.clk(in_1), .D(d_ff_2_q), .Q(d_ff_3_q), .Qn(d_ff_3_qn), .preset(in_2), .reset(in_4));
  // Probe on d_ff_3_qn
  // Probe on d_ff_4_q
  D_Flip_Flop d_ff_4 (.clk(in_1), .D(d_ff_3_q), .Q(d_ff_4_q), .Qn(d_ff_4_qn), .preset(in_2), .reset(in_4));
  // Probe on d_ff_4_qn
  // Probe on d_ff_5_q
  D_Flip_Flop d_ff_5 (.clk(in_1), .D(d_ff_4_q), .Q(d_ff_5_q), .Qn(d_ff_5_qn), .preset(in_2), .reset(in_4));
  // Probe on d_ff_5_qn
  // Probe on d_ff_6_q
  D_Flip_Flop d_ff_6 (.clk(in_1), .D(d_ff_5_q), .Q(d_ff_6_q), .Qn(d_ff_6_qn), .preset(in_2), .reset(in_4));
  // Probe on d_ff_6_qn
endmodule
