// Logisim project Questão 7.circ as structural Verilog: 1 circuit, main circuit main
module main (
  input  in_1,
  input  in_2,
  input  in_3,
  input  in_4,
  input  in_5,
  input  in_6,
  input  in_7,
  input  in_8,
  input  in_9,
  output out_10,
  output out_11,
  output out_12,
  output out_13,
  output out_14,
  output out_15,
  output out_16,
  output out_17,
  output out_18,
  output out_19,
  output out_20,
  output out_21,
  output out_22,
  output out_23,
  output out_24,
  output out_25,
  output out_26
);

  wire or_1_out, or_2_out, or_3_out, or_7_out, or_8_out;

  not not_1 (out_17, in_4);
  not not_2 (out_23, in_7);
  or or_1 (or_1_out, out_25, in_9, in_8);
  not not_3 (out_10, in_1);
  or or_2 (or_2_out, out_13, or_7_out, in_2);
  or or_3 (or_3_out, out_19, or_8_out, in_5);
  not not_4 (out_19, in_5);
  not not_5 (out_25, in_8);
  not not_6 (out_13, in_2);
  not not_7 (out_15, in_3);
  or or_4 (out_15, out_17, in_4, or_3_out);
  not not_8 (out_21, in_6);
  or or_5 (out_21, out_23, in_7, or_1_out);
  or or_6 (out_11, out_10, or_2_out, in_1);
  or or_7 (or_7_out, out_15, out_15, in_3);
  ExactlyOne xor_1 (.out(out_16), .in0(in_3), .in2(out_15), .in4(out_15));
  ExactlyOne xor_2 (.out(out_18), .in0(out_17), .in2(in_4), .in4(or_3_out));
  ExactlyOne xor_3 (.out(out_20), .in0(out_19), .in2(or_8_out), .in4(in_5));
  or or_8 (or_8_out, out_21, out_21, in_6);
  ExactlyOne xor_4 (.out(out_22), .in0(in_6), .in2(out_21), .in4(out_21));
  ExactlyOne xor_5 (.out(out_24), .in0(out_23), .in2(in_7), .in4(or_1_out));
  ExactlyOne xor_6 (.out(out_26), .in0(out_25), .in2(in_9), .in4(in_8));
  ExactlyOne xor_7 (.out(out_12), .in0(out_10), .in2(in_1), .in4(or_2_out));
  ExactlyOne xor_8 (.out(out_14), .in0(out_13), .in2(or_7_out), .in4(in_2));
endmodule
