// Logisim project Projeto.circ as structural Verilog: 5 circuits, main circuit main
module Complemento_de_2 (
  input  [3:0] in_1,
  output [3:0] out_2
);

  wire meio_somador_2_out_3, meio_somador_3_out_3, meio_somador_4_out_3;

  Meio_Somador meio_somador_1 (.in_1(meio_somador_2_out_3), .in_2(in_1[3]), .out_4(out_2[3]));  // open: out_3
  Meio_Somador meio_somador_2 (
    .in_1(meio_somador_3_out_3), .in_2(in_1[2]), .out_3(meio_somador_2_out_3), .out_4(out_2[2]));
  Meio_Somador meio_somador_3 (
    .in_1(meio_somador_4_out_3), .in_2(in_1[1]), .out_3(meio_somador_3_out_3), .out_4(out_2[1]));
  Meio_Somador meio_somador_4 (.in_1(1'b1), .in_2(in_1[0]), .out_3(meio_somador_4_out_3), .out_4(out_2[0]));
endmodule

module main (
  input  in_1,
  input  in_2,
  input  [3:0] in_3,
  output out_4
);

  wire clock_1_out, d_ff_1_q, d_ff_2_q, d_ff_3_q, not_1_out, not_2_out, not_3_out, not_4_out;
  wire [3:0] complemento_de_2_1_out_2, d_ff_4_qn, somador_de_4_bits_1_out_3;

  Clock clock_1 (.out(clock_1_out));
  D_Flip_Flop d_ff_1 (.clk(clock_1_out), .D(in_1), .Q(d_ff_1_q), .Qn(d_ff_4_qn[3]), .reset(in_2));  // open: preset
  D_Flip_Flop d_ff_2 (.clk(clock_1_out), .D(d_ff_1_q), .Q(d_ff_2_q), .Qn(d_ff_4_qn[2]), .reset(in_2));  // open: preset
  D_Flip_Flop d_ff_3 (.clk(clock_1_out), .D(d_ff_2_q), .Q(d_ff_3_q), .Qn(d_ff_4_qn[1]), .reset(in_2));  // open: preset
  D_Flip_Flop d_ff_4 (.clk(clock_1_out), .D(d_ff_3_q), .Qn(d_ff_4_qn[0]), .reset(in_2));  // open: Q, preset
  Complemento_de_2 complemento_de_2_1 (.in_1(d_ff_4_qn), .out_2(complemento_de_2_1_out_2));
  not not_1 (not_1_out, somador_de_4_bits_1_out_3[2]);
  not not_2 (not_2_out, somador_de_4_bits_1_out_3[3]);
  Somador_de_4_bits somador_de_4_bits_1 (
    .in_1(complemento_de_2_1_out_2), .in_2(in_3), .out_3(somador_de_4_bits_1_out_3));
  not not_3 (not_3_out, somador_de_4_bits_1_out_3[1]);
  not not_4 (not_4_out, somador_de_4_bits_1_out_3[0]);
  and and_1 (out_4, not_2_out, not_1_out, not_3_out, not_4_out);
endmodule

module Meio_Somador (
  input  in_1,
  input  in_2,
  output out_3,
  output out_4
);

  and and_1 (out_3, in_2, in_1);
  xor xor_1 (out_4, in_1, in_2);
endmodule

module Somador (
  input  in_1,
  input  in_2,
  input  in_3,
  output out_4,
  output out_5
);

  wire meio_somador_1_out_3, meio_somador_1_out_4, meio_somador_2_out_3;

  Meio_Somador meio_somador_1 (.in_1(in_1), .in_2(in_2), .out_3(meio_somador_1_out_3), .out_4(meio_somador_1_out_4));
  Meio_Somador meio_somador_2 (.in_1(meio_somador_1_out_4), .in_2(in_3), .out_3(meio_somador_2_out_3), .out_4(out_4));
  or or_1 (out_5, meio_somador_2_out_3, meio_somador_1_out_3);
endmodule

module Somador_de_4_bits (
  input  [3:0] in_1,
  input  [3:0] in_2,
  output [3:0] out_3
);

  wire somador_1_out_5, somador_3_out_5, somador_4_out_5;

  Somador somador_1 (.in_1(somador_3_out_5), .in_2(in_2[2]), .in_3(in_1[2]), .out_4(out_3[2]), .out_5(somador_1_out_5));
  Somador somador_2 (.in_1(somador_1_out_5), .in_2(in_2[3]), .in_3(in_1[3]), .out_4(out_3[3]));  // open: out_5
  Somador somador_3 (.in_1(somador_4_out_5), .in_2(in_2[1]), .in_3(in_1[1]), .out_4(out_3[1]), .out_5(somador_3_out_5));
  Somador somador_4 (.in_1(1'b0), .in_2(in_2[0]), .in_3(in_1[0]), .out_4(out_3[0]), .out_5(somador_4_out_5));
endmodule
