// Logisim project Somador de dois Bits.circ as structural Verilog: 1 circuit, main circuit main
module main (
  input  in_1,
  input  in_2,
  input  in_3,
  input  in_4,
  input  in_5,
  input  in_6,
  output out_7,
  output out_8,
  output out_9,
  output out_10,
  output out_11
);

  wire and_2_out;

  and and_1 (out_10, in_5, in_6);
  xor xor_1 (out_11, in_6, in_5);
  and and_2 (and_2_out, in_2, in_2, in_4);
  xor xor_2 (out_9, in_2, in_4);
  and and_3 (out_7, in_3, in_1, and_2_out);
  or or_1 (out_8, and_2_out, in_1, in_3);
endmodule
